// Logisim project ALU.circ as structural Verilog: 15 circuits, main circuit ALU32
module LeftShift32 (
  input  [31:0] B,
  input  Cin,
  input  [4:0] Sa,
  output [31:0] C
);

  wire [31:0] eight_bit_shifter_1_shifted, four_bit_shifter_1_shifted, multiplexer_1_out, multiplexer_2_out,
       multiplexer_3_out, multiplexer_4_out, one_bit_shifter_1_shifted, sixteen_bit_shifter_1_shifted,
       two_bit_shifter_1_shifted;

  one_bit_shifter one_bit_shifter_1 (.C_in(Cin), .B(B), .shifted(one_bit_shifter_1_shifted));
  Multiplexer #(.width(32), .enable("false")) multiplexer_1 (
    .in0(B), .in1(one_bit_shifter_1_shifted), .out(multiplexer_1_out), .sel(Sa[0]));
  Multiplexer #(.width(32), .enable("false")) multiplexer_2 (
    .in0(multiplexer_1_out), .in1(two_bit_shifter_1_shifted), .out(multiplexer_2_out), .sel(Sa[1]));
  two_bit_shifter two_bit_shifter_1 (.C_in(Cin), .B(multiplexer_1_out), .shifted(two_bit_shifter_1_shifted));
  Multiplexer #(.width(32), .enable("false")) multiplexer_3 (
    .in0(multiplexer_2_out), .in1(four_bit_shifter_1_shifted), .out(multiplexer_3_out), .sel(Sa[2]));
  four_bit_shifter four_bit_shifter_1 (.C_in(Cin), .B(multiplexer_2_out), .shifted(four_bit_shifter_1_shifted));
  eight_bit_shifter eight_bit_shifter_1 (.C_in(Cin), .B(multiplexer_3_out), .shifted(eight_bit_shifter_1_shifted));
  Multiplexer #(.width(32), .enable("false")) multiplexer_4 (
    .in0(multiplexer_3_out), .in1(eight_bit_shifter_1_shifted), .out(multiplexer_4_out), .sel(Sa[3]));
  sixteen_bit_shifter sixteen_bit_shifter_1 (
    .C_in(Cin), .B(multiplexer_4_out), .Shifted(sixteen_bit_shifter_1_shifted));
  Multiplexer #(.width(32), .enable("false")) multiplexer_5 (
    .in0(multiplexer_4_out), .in1(sixteen_bit_shifter_1_shifted), .out(C), .sel(Sa[4]));

  // Notes on the sheet:
  //   left 32 bit shifter
endmodule

module ALU32 (
  input  [31:0] A,
  input  [31:0] B,
  input  [4:0] Sa,
  input  [3:0] Op,
  output [31:0] C,
  output V
);

  wire add32_1_v, add_out, and_8640e961_out, comparator_1_eq, comparator_1_gt, comparator_1_lt, eq_out,
       gt_out, le_out, ne_out, nor_0e33f0e5_out, not_1_out, not_2_out, not_3_out, not_4_out, not_5_out,
       or_92535c4c_out, shift_left_logical_out, shift_right_out, subtract32_1_v, subtract_out,
       xor_0044f627_out;
  wire [31:0] add32_1_c, and_1_out, bit_extender_1_out, bit_extender_2_out, bit_extender_3_out,
       bit_extender_4_out, leftshift32_1_c, nor_1_out, or_1_out, rightshift32_1_c, subtract32_1_c, xor_1_out;

  assign and_1_out = A & B;  // AND_Gate and_1, 32 bits wide
  assign or_1_out = A | B;  // OR_Gate or_1, 32 bits wide
  assign xor_1_out = A ^ B;  // XOR_Gate xor_1, 32 bits wide
  assign nor_1_out = ~(A | B);  // NOR_Gate nor_1, 32 bits wide
  Comparator #(.width(32)) comparator_1 (
    .a(A), .b(B), .gt(comparator_1_gt), .eq(comparator_1_eq), .lt(comparator_1_lt));
  Add32 add32_1 (.A(A), .B(B), .C(add32_1_c), .V(add32_1_v));  // open: Cin
  Subtract32 subtract32_1 (.A(A), .B(B), .C(subtract32_1_c), .V(subtract32_1_v));
  not not_1 (not_1_out, Op[3]);
  not not_2 (not_2_out, Op[2]);
  not not_3 (not_3_out, Op[1]);
  not not_4 (not_4_out, Op[0]);
  LeftShift32 leftshift32_1 (.B(B), .Sa(Sa), .C(leftshift32_1_c));  // open: Cin
  RightShift32 rightshift32_1 (.Op(Op[0]), .Sa(Sa), .B(B), .C(rightshift32_1_c));
  not not_5 (not_5_out, comparator_1_eq);
  and and_8640e961 (and_8640e961_out, not_1_out, not_2_out, not_3_out, not_4_out);
  and or_92535c4c (or_92535c4c_out, not_1_out, not_2_out, not_3_out, Op[0]);
  and shift_left_logical (shift_left_logical_out, not_1_out, not_2_out, Op[1]);
  and xor_0044f627 (xor_0044f627_out, not_4_out, not_3_out, Op[2], not_1_out);
  and nor_0e33f0e5 (nor_0e33f0e5_out, Op[0], not_3_out, Op[2], not_1_out);
  and shift_right (shift_right_out, not_1_out, Op[2], Op[1]);
  and ne (ne_out, Op[3], not_2_out, not_3_out, not_4_out);
  and eq (eq_out, Op[3], not_2_out, not_3_out, Op[0]);
  and le (le_out, Op[3], not_2_out, Op[1], not_4_out);
  and gt (gt_out, Op[3], not_2_out, Op[1], Op[0]);
  and subtract (subtract_out, Op[3], Op[2], not_3_out);
  and add (add_out, Op[3], Op[2], Op[1]);
  assign bit_extender_1_out = {{31{not_5_out}}, not_5_out};  // Bit_Extender bit_extender_1
  assign bit_extender_2_out = {{31{comparator_1_eq}}, comparator_1_eq};  // Bit_Extender bit_extender_2
  assign bit_extender_3_out = {{31{comparator_1_lt}}, comparator_1_lt};  // Bit_Extender bit_extender_3
  assign bit_extender_4_out = {{31{comparator_1_gt}}, comparator_1_gt};  // Bit_Extender bit_extender_4
  Multiplexer #(.enable("false")) multiplexer_1 (.in0(subtract32_1_v), .in1(add32_1_v), .out(V), .sel(Op[1]));
  Multiplexer #(.width(32), .enable("false")) multiplexer_2 (
    .in1(and_1_out), .out(C), .sel(and_8640e961_out));  // open: in0
  Multiplexer #(.width(32), .enable("false")) multiplexer_3 (
    .in1(or_1_out), .out(C), .sel(or_92535c4c_out));  // open: in0
  Multiplexer #(.width(32), .enable("false")) multiplexer_4 (
    .in1(leftshift32_1_c), .out(C), .sel(shift_left_logical_out));  // open: in0
  Multiplexer #(.width(32), .enable("false")) multiplexer_5 (
    .in1(xor_1_out), .out(C), .sel(xor_0044f627_out));  // open: in0
  Multiplexer #(.width(32), .enable("false")) multiplexer_6 (
    .in1(nor_1_out), .out(C), .sel(nor_0e33f0e5_out));  // open: in0
  Multiplexer #(.width(32), .enable("false")) multiplexer_7 (
    .in1(rightshift32_1_c), .out(C), .sel(shift_right_out));  // open: in0
  Multiplexer #(.width(32), .enable("false")) multiplexer_8 (
    .in1(bit_extender_1_out), .out(C), .sel(ne_out));  // open: in0
  Multiplexer #(.width(32), .enable("false")) multiplexer_9 (
    .in1(bit_extender_2_out), .out(C), .sel(eq_out));  // open: in0
  Multiplexer #(.width(32), .enable("false")) multiplexer_10 (
    .in1(bit_extender_3_out), .out(C), .sel(le_out));  // open: in0
  Multiplexer #(.width(32), .enable("false")) multiplexer_11 (
    .in1(bit_extender_4_out), .out(C), .sel(gt_out));  // open: in0
  Multiplexer #(.width(32), .enable("false")) multiplexer_12 (
    .in1(subtract32_1_c), .out(C), .sel(subtract_out));  // open: in0
  Multiplexer #(.width(32), .enable("false")) multiplexer_13 (.in1(add32_1_c), .out(C), .sel(add_out));  // open: in0

  // Notes on the sheet:
  //   The right shifter isn't
  //   like a left shifter and done
  //   all over again, but uses the
  //   left shifter by transforming
  //   the inputs and outputs to it.
  //   same thing with subtracter.
endmodule

module one_bit_shifter (
  input  C_in,
  input  [31:0] B,
  output [31:0] shifted
);


  assign shifted = {B[30:0], C_in};

  // Notes on the sheet:
  //   one bit shifter
endmodule

module Add32 (
  input  [31:0] A,
  input  [31:0] B,
  input  Cin,
  output [31:0] C,
  output V
);

  wire sixteen_bit_adder_1_cout;

  sixteen_bit_adder sixteen_bit_adder_1 (
    .A16(A[15:0]), .B16(B[15:0]), .Cin(Cin), .Cout(sixteen_bit_adder_1_cout), .sum(C[15:0]));
  sixteen_bit_adder sixteen_bit_adder_2 (
    .A16(A[31:16]), .B16(B[31:16]), .Cin(sixteen_bit_adder_1_cout), .Cout(V), .sum(C[31:16]));
endmodule

module two_bit_shifter (
  input  C_in,
  input  [31:0] B,
  output [31:0] shifted
);

  wire [31:0] one_bit_shifter_1_shifted;

  one_bit_shifter one_bit_shifter_1 (.C_in(C_in), .B(B), .shifted(one_bit_shifter_1_shifted));
  one_bit_shifter one_bit_shifter_2 (.C_in(C_in), .B(one_bit_shifter_1_shifted), .shifted(shifted));

  // Notes on the sheet:
  //   two bit shifter
endmodule

module four_bit_shifter (
  input  C_in,
  input  [31:0] B,
  output [31:0] shifted
);

  wire [31:0] two_bit_shifter_1_shifted;

  two_bit_shifter two_bit_shifter_1 (.C_in(C_in), .B(B), .shifted(two_bit_shifter_1_shifted));
  two_bit_shifter two_bit_shifter_2 (.C_in(C_in), .B(two_bit_shifter_1_shifted), .shifted(shifted));

  // Notes on the sheet:
  //   four bit shifter
endmodule

module eight_bit_shifter (
  input  C_in,
  input  [31:0] B,
  output [31:0] shifted
);

  wire [31:0] four_bit_shifter_1_shifted;

  four_bit_shifter four_bit_shifter_1 (.C_in(C_in), .B(B), .shifted(four_bit_shifter_1_shifted));
  four_bit_shifter four_bit_shifter_2 (.C_in(C_in), .B(four_bit_shifter_1_shifted), .shifted(shifted));

  // Notes on the sheet:
  //   eight bit shifter
endmodule

module sixteen_bit_shifter (
  input  C_in,
  input  [31:0] B,
  output [31:0] Shifted
);

  wire [31:0] eight_bit_shifter_1_shifted;

  eight_bit_shifter eight_bit_shifter_1 (.C_in(C_in), .B(B), .shifted(eight_bit_shifter_1_shifted));
  eight_bit_shifter eight_bit_shifter_2 (.C_in(C_in), .B(eight_bit_shifter_1_shifted), .shifted(Shifted));

  // Notes on the sheet:
  //   sixteen bit shifter
endmodule

module one_bit_adder (
  input  A,
  input  B,
  input  Cin,
  output S,
  output Cout
);

  wire and_1_out, and_2_out, xor_1_out;

  xor xor_1 (xor_1_out, A, B);
  and and_1 (and_1_out, xor_1_out, Cin);
  and and_2 (and_2_out, A, B);
  xor xor_2 (S, xor_1_out, Cin);
  or or_1 (Cout, and_1_out, and_2_out);

  // Notes on the sheet:
  //   1-bit adder
endmodule

module four_bit_adder (
  input  [3:0] A4,
  input  [3:0] B4,
  input  Cin,
  output Cout,
  output [3:0] S4
);

  wire one_bit_adder_1_cout, one_bit_adder_2_cout, one_bit_adder_3_cout;

  one_bit_adder one_bit_adder_1 (.A(A4[0]), .B(B4[0]), .Cin(Cin), .S(S4[0]), .Cout(one_bit_adder_1_cout));
  one_bit_adder one_bit_adder_2 (
    .A(A4[1]), .B(B4[1]), .Cin(one_bit_adder_1_cout), .S(S4[1]), .Cout(one_bit_adder_2_cout));
  one_bit_adder one_bit_adder_3 (
    .A(A4[2]), .B(B4[2]), .Cin(one_bit_adder_2_cout), .S(S4[2]), .Cout(one_bit_adder_3_cout));
  one_bit_adder one_bit_adder_4 (.A(A4[3]), .B(B4[3]), .Cin(one_bit_adder_3_cout), .S(S4[3]), .Cout(Cout));
endmodule

module sixteen_bit_adder (
  input  [15:0] A16,
  input  [15:0] B16,
  input  Cin,
  output Cout,
  output [15:0] sum
);

  wire four_bit_adder_1_cout, four_bit_adder_2_cout, four_bit_adder_3_cout;

  four_bit_adder four_bit_adder_1 (
    .A4(A16[3:0]), .B4(B16[3:0]), .Cin(Cin), .Cout(four_bit_adder_1_cout), .S4(sum[3:0]));
  four_bit_adder four_bit_adder_2 (
    .A4(A16[7:4]), .B4(B16[7:4]), .Cin(four_bit_adder_1_cout), .Cout(four_bit_adder_2_cout), .S4(sum[7:4]));
  four_bit_adder four_bit_adder_3 (
    .A4(A16[11:8]), .B4(B16[11:8]), .Cin(four_bit_adder_2_cout), .Cout(four_bit_adder_3_cout), .S4(sum[11:8]));
  four_bit_adder four_bit_adder_4 (
    .A4(A16[15:12]), .B4(B16[15:12]), .Cin(four_bit_adder_3_cout), .Cout(Cout), .S4(sum[15:12]));
endmodule

module RightShift32 (
  input  Op,
  input  [4:0] Sa,
  input  [31:0] B,
  output [31:0] C
);

  wire multiplexer_1_out;

  Multiplexer #(.enable("false")) multiplexer_1 (.in1(B[31]), .out(multiplexer_1_out), .sel(Op));  // open: in0
  LeftShift32 leftshift32_1 (
    .B({B[0], B[1], B[2], B[3], B[4], B[5], B[6], B[7], B[8], B[9], B[10], B[11], B[12], B[13], B[14], B[15], B[16], B[17], B[18], B[19], B[20], B[21], B[22], B[23], B[24], B[25], B[26], B[27], B[28], B[29], B[30], B[31]}),
    .Cin(multiplexer_1_out), .Sa(Sa),
    .C({C[0], C[1], C[2], C[3], C[4], C[5], C[6], C[7], C[8], C[9], C[10], C[11], C[12], C[13], C[14], C[15], C[16], C[17], C[18], C[19], C[20], C[21], C[22], C[23], C[24], C[25], C[26], C[27], C[28], C[29], C[30], C[31]}));
endmodule

module testing (
  input  [31:0] A,
  input  [31:0] B,
  output [31:0] C
);

  assign C = A;  // AND_Gate and_1, 32 bits wide AND_Gate
endmodule

module Subtract32 (
  input  [31:0] A,
  input  [31:0] B,
  output [31:0] C,
  output V
);

  wire add32_2_v, comparator_1_eq, xor_1_out;
  wire [31:0] add32_1_c, not_1_out;

  assign not_1_out = ~B;  // NOT_Gate not_1, 32 bits wide
  Comparator #(.width(1)) comparator_1 (.a(add32_2_v), .b(B[31]), .eq(comparator_1_eq));  // open: gt, lt
  xor xor_1 (xor_1_out, A[31], B[31]);
  Add32 add32_1 (.A(32'h1), .B(not_1_out), .C(add32_1_c));  // open: Cin, V
  and and_1 (V, comparator_1_eq, xor_1_out);
  Add32 add32_2 (.A(A), .B(add32_1_c), .C(C), .V(add32_2_v));  // open: Cin

  // Notes on the sheet:
  //   then there's overflow.
  //   overflow handling for subtraction:
  //   If A's sign and B's sign aren't equal
  //   and C's sign equals B's sign,
endmodule

module test_subtract (
  input  [31:0] A,
  input  [31:0] B,
  output [31:0] C,
  output V
);

  wire add32_2_v, comparator_1_eq, comparator_2_eq, or_1_out, xor_1_out;
  wire [31:0] add32_1_c, not_1_out;

  assign not_1_out = ~B;  // NOT_Gate not_1, 32 bits wide
  Comparator #(.width(1)) comparator_1 (.a(C[31]), .b(B[31]), .eq(comparator_1_eq));  // open: gt, lt
  Comparator #(.width(1)) comparator_2 (.a(add32_2_v), .b(B[31]), .eq(comparator_2_eq));  // open: gt, lt
  xor xor_1 (xor_1_out, A[31], B[31]);
  or or_1 (or_1_out, comparator_1_eq, comparator_2_eq);
  Add32 add32_1 (.A(32'h1), .B(not_1_out), .C(add32_1_c));  // open: Cin, V
  Add32 add32_2 (.A(A), .B(add32_1_c), .C(C), .V(add32_2_v));  // open: Cin
  and and_1 (V, or_1_out, xor_1_out);

  // Notes on the sheet:
  //   then there's overflow.
  //   overflow handling for subtraction:
  //   If A's sign and B's sign aren't equal
  //   and C's sign equals B's sign,
endmodule
